# Fritzing sketch LaserReceiverPhotoTransistor (saved by Fritzing 0.8.5b)
circuit board: 3.20495cm x 2.5552cm
breadboards: 1

parts:
  U1 = LM 358 Dual Op-Amp [package="DIP8 [THT]"]
  R1 = Resistor [tolerance=±5% resistance=4.7k package=THT]
  R3 = Resistor [tolerance=±5% resistance=2.2k package=THT]
  J1(Rx) = female pin header, 1 pin [form="♀ (female)"]
  R2 = Resistor [tolerance=±5% resistance=330k package=THT]
  P1 = S1133 Si Photodiode [part_number=PhotoTransistor package="8mm Ceramic [THT]"]
  R4 = Resistor [tolerance=±5% resistance=470k package=THT]
  R5 = Resistor [tolerance=±5% resistance=470k package=THT]

nets:
  N1: U1.connector0, J1(Rx).pin1, R2.Pin_1
  N2: U1.connector1, R1.Pin_1, R2.Pin_0
  N3: U1.connector2, R4.Pin_0, R5.Pin_1
  GND: U1.connector3, P1.cathode, R4.Pin_1
  5V: U1.connector7, R3.Pin_1, R5.Pin_0
  N4: R1.Pin_0, R3.Pin_0, P1.anode

notes:
  1
  2
  3
  4
  5
