# Fritzing sketch LaserReceiverTransistor (saved by Fritzing 0.8.5b)
breadboards: 1

parts:
  R2 = Resistor [tolerance=±5% resistance=10k package=THT]
  P2 = S1133 Si Photodiode [package="8mm Ceramic [THT]"]
  R1 = Resistor [tolerance=±5% resistance=200k package=THT]
  J1_(Rx) = female pin header, 1 pin [form="♀ (female)"]
  R3 = Resistor [tolerance=±5% resistance=10k package=THT]
  Q2 = Basic FET N-Channel [package="TO220 [THT]"]
  Q1 = Basic FET N-Channel [package="TO220 [THT]"]

nets:
  3.3V: R2.Pin_0, P2.cathode, R3.Pin_0
  N1: R2.Pin_1, Q2.gate, Q1.drain
  N2: P2.anode, R1.Pin_0, Q1.gate
  GND: R1.Pin_1, Q2.source, Q1.source
  N3: J1_(Rx).pin1, R3.Pin_1, Q2.drain
